# Fritzing sketch SON (saved by Fritzing 0.9.3b)
breadboards: 1

parts:
  part = Water Level Sensor
  U3 = RELAY-SOLIDSTATE [package=relay-s108t02]
  Part6 = InvenSense MPU6050
  Start_Button = Round Pushbutton
  LED1 = LED - 5mm [color="Red (633nm)" package="5 mm [THT]"]
  J1 = Piezo Speaker
  AC_Filter_Pump = Vibration Motor- ROB-08449 [package=vibe-motor-10mm]
  DC_Motor_-_Thruster2 = Vibration Motor- ROB-08449 [package=vibe-motor-10mm]
  R1 = Resistor [tolerance=±5% resistance=220 package="2512 [SMD]"]  # not connected
  Water_Level_Sensor2 = Water Level Sensor
  DC_Motor_-_Thruster1 = Vibration Motor- ROB-08449 [package=vibe-motor-10mm]
  HLK-PM1 = HLK-PM12 [part_number=HLK-PM12]
  HLK-PM2 = HLK-PM01
  Part7 = Arduino Uno (Rev3) - ICSP
  AC_Power_Supply_-_220V = Lilypad Battery Connect
  S3 = H-Bridge with L298N
  R2 = Resistor [tolerance=±5% resistance=220 package="2512 [SMD]"]
  R3 = Resistor [tolerance=±5% resistance=220 package="2512 [SMD]"]

nets:
  N1: part.SIG, Part7.A5/SCL
  VCC: part.VCC, Water_Level_Sensor2.VCC, HLK-PM2.+Vo
  GND: part.GND, Water_Level_Sensor2.GND, HLK-PM2.-Vo
  N2: U3.T1, AC_Filter_Pump.+, HLK-PM1.AC_2, HLK-PM2.AC#0, AC_Power_Supply_-_220V.-
  N3: U3.T2, AC_Filter_Pump.-
  N4: U3.+, Part7.D11_PWM/MOSI
  GND_2: U3.-, Part6.GND, Start_Button.leg0, LED1.cathode, J1.pin1, Part7.GND
  VCC_2: Part6.VCC, Part7.5V, R3.Pin_1
  N5: Part6.SCL, Part7.A3
  N6: Part6.SDA, Part7.A4/SDA
  N7: Part6.INT, Part7.D3_PWM
  N8: Start_Button.leg1, Part7.D4, R3.Pin_0
  N9: LED1.anode, R2.Pin_0
  N10: J1.pin2, Part7.D13/SCK
  N11: DC_Motor_-_Thruster2.+, S3.M1-01
  N12: DC_Motor_-_Thruster2.-, S3.M1-02
  N13: Water_Level_Sensor2.SIG, Part7.D2
  N14: DC_Motor_-_Thruster1.+, S3.M2-01
  N15: DC_Motor_-_Thruster1.-, S3.M2-02
  N16: HLK-PM1.AC_1, HLK-PM2.AC#1, AC_Power_Supply_-_220V.+
  N17: HLK-PM1.-Vo, S3.GND
  N18: HLK-PM1.+Vo, S3.12V
  N19: Part7.D8, S3.ENB
  N20: Part7.D9_PWM, S3.IN1
  N21: Part7.D10_PWM/SS, S3.IN2
  N22: Part7.D12/MISO, R2.Pin_1
  N23: Part7.D5_PWM, S3.IN3
  N24: Part7.D6_PWM, S3.IN4
  N25: Part7.D7, S3.ENA

custom parts:
  Water Level Sensor: A water level sensor. This sensor operates at 3V to 5V. The Sig (signal) pin outputs an analogue signal that is in proportion to the amount of water in contact with the sensor.
  H-Bridge with L298N: h-bridge
